// Logisim project tragamonedas.circ as structural Verilog: 8 circuits, main circuit main
module main (
  input  [1:0] in_1,
  input  [1:0] Resultados,
  input  [1:0] in_3,
  input  Hay_Premio,
  input  Hay_Creditos,
  output _11___Victoria,
  output out_7
);

  wire and_1_out, and_2_out, Animacion_Terminada_out, clock_1_out, controlador_animacion_1_display_1,
       controlador_animacion_1_display_2, controlador_animacion_1_display_3,
       Controlador_Palanca_deteccion_palanca, Controlador_Palanca_influye, Controlador_Palanca_salida,
       not_1_out, not_2_out, Victoria_Terminada_out;
  wire [1:0] joystick_1_y;
  wire [6:0] controlador_display_1_columna_1, controlador_display_1_columna_2,
       controlador_display_1_columna_3, controlador_display_1_columna_4, controlador_display_1_columna_5,
       controlador_display_2_columna_1, controlador_display_2_columna_2, controlador_display_2_columna_3,
       controlador_display_2_columna_4, controlador_display_2_columna_5, controlador_display_3_columna_1,
       controlador_display_3_columna_2, controlador_display_3_columna_3, controlador_display_3_columna_4,
       controlador_display_3_columna_5;

  Clock clock_1 (.out(clock_1_out));
  Button Victoria_Terminada (.out(Victoria_Terminada_out));
  Button Animacion_Terminada (.out(Animacion_Terminada_out));
  DotMatrix dotmatrix_1 (
    .col0(controlador_display_1_columna_1), .col1(controlador_display_1_columna_2),
    .col2(controlador_display_1_columna_3), .col3(controlador_display_1_columna_4),
    .col4(controlador_display_1_columna_5));
  controlador_display controlador_display_1 (
    .Resultado(in_1), .Detener(controlador_animacion_1_display_1),
    .Columna_1(controlador_display_1_columna_1), .Columna_2(controlador_display_1_columna_2),
    .Columna_3(controlador_display_1_columna_3), .Columna_4(controlador_display_1_columna_4),
    .Columna_5(controlador_display_1_columna_5));
  maquina_estados maquina_estados_1 (
    .Reloj(clock_1_out), .Victoria_Terminada(Victoria_Terminada_out),
    .Nueva_Tirada(Controlador_Palanca_salida), .Hay_Creditos(Hay_Creditos),
    .Animacion_Terminada(Animacion_Terminada_out), .Hay_Premio(Hay_Premio), .out_7(_11___Victoria),
    .out_8(out_7));
  DotMatrix dotmatrix_2 (
    .col0(controlador_display_2_columna_1), .col1(controlador_display_2_columna_2),
    .col2(controlador_display_2_columna_3), .col3(controlador_display_2_columna_4),
    .col4(controlador_display_2_columna_5));
  controlador_display controlador_display_2 (
    .Resultado(Resultados), .Detener(controlador_animacion_1_display_2),
    .Columna_1(controlador_display_2_columna_1), .Columna_2(controlador_display_2_columna_2),
    .Columna_3(controlador_display_2_columna_3), .Columna_4(controlador_display_2_columna_4),
    .Columna_5(controlador_display_2_columna_5));
  Joystick #(.bits(2)) joystick_1 (.y(joystick_1_y));  // open: x
  not not_1 (not_1_out, out_7);
  not not_2 (not_2_out, _11___Victoria);
  and and_1 (and_1_out, not_1_out, not_2_out, Hay_Creditos);
  controlador_palanca Controlador_Palanca (
    .Palanca(joystick_1_y), .Habilitar(and_1_out), .Salida(Controlador_Palanca_salida),
    .Influye(Controlador_Palanca_influye), .Deteccion_Palanca(Controlador_Palanca_deteccion_palanca));
  DotMatrix dotmatrix_3 (
    .col0(controlador_display_3_columna_1), .col1(controlador_display_3_columna_2),
    .col2(controlador_display_3_columna_3), .col3(controlador_display_3_columna_4),
    .col4(controlador_display_3_columna_5));
  controlador_display controlador_display_3 (
    .Resultado(in_3), .Detener(controlador_animacion_1_display_3),
    .Columna_1(controlador_display_3_columna_1), .Columna_2(controlador_display_3_columna_2),
    .Columna_3(controlador_display_3_columna_3), .Columna_4(controlador_display_3_columna_4),
    .Columna_5(controlador_display_3_columna_5));
  LED Influye (.in(Controlador_Palanca_influye));
  LED \Detección_Palanca  (.in(Controlador_Palanca_deteccion_palanca));
  controlador_animacion controlador_animacion_1 (
    .Palanca(and_2_out), .Display_1(controlador_animacion_1_display_1),
    .Display_2(controlador_animacion_1_display_2), .Display_3(controlador_animacion_1_display_3));
  and and_2 (and_2_out, Controlador_Palanca_influye, Controlador_Palanca_salida);

  // Notes on the sheet:
  //   Harcodeados
  //   Controlador
  //   Display
  //   Maquina de
  //   estados
  //   00 - Espera
  //   01 - Juego
  //   Controlador
  //   Display
  //   Controlador
  //   Display
  //   Controlador
  //   Animacion
endmodule

module controlador_display (
  input  [1:0] Resultado,
  input  Detener,
  output [6:0] Columna_1,
  output [6:0] Columna_2,
  output [6:0] Columna_3,
  output [6:0] Columna_4,
  output [6:0] Columna_5
);

  wire clock_1_out;
  wire [1:0] multiplexer_1_out, Simbolo_Animacion_q;

  Clock clock_1 (.out(clock_1_out));
  Counter #(.width(2), .max('h2)) Simbolo_Animacion (
    .Q(Simbolo_Animacion_q), .clk(clock_1_out));  // open: load, D, count, carry, clr
  Multiplexer #(.width(2), .enable("false")) multiplexer_1 (
    .in0(Simbolo_Animacion_q), .in1(Resultado), .out(multiplexer_1_out), .sel(Detener));
  ROM #(.addrWidth(2), .dataWidth(7)) rom_1 (.addr(multiplexer_1_out), .data(Columna_1));  // open: sel
  ROM #(.addrWidth(2), .dataWidth(7)) rom_2 (.addr(multiplexer_1_out), .data(Columna_2));  // open: sel
  ROM #(.addrWidth(2), .dataWidth(7)) rom_3 (.addr(multiplexer_1_out), .data(Columna_3));  // open: sel
  ROM #(.addrWidth(2), .dataWidth(7)) rom_4 (.addr(multiplexer_1_out), .data(Columna_4));  // open: sel
  ROM #(.addrWidth(2), .dataWidth(7)) rom_5 (.addr(multiplexer_1_out), .data(Columna_5));  // open: sel

  // Notes on the sheet:
  //   contents of rom_1 (hex, n*v repeats v):
  //   40 6 8
  //   contents of rom_2 (hex, n*v repeats v):
  //   43 3e 1b
  //   contents of rom_3 (hex, n*v repeats v):
  //   4c 7f 3e
  //   contents of rom_4 (hex, n*v repeats v):
  //   58 3e 6c
  //   contents of rom_5 (hex, n*v repeats v):
  //   60 6 8
endmodule

module controlador_palanca (
  input  [1:0] Palanca,
  input  Habilitar,
  output Deteccion_Palanca,
  output Salida,
  output Influye
);

  wire not_1_out;

  and and_1 (Deteccion_Palanca, Palanca[0], Palanca[1]);
  D_Flip_Flop d_ff_1 (
    .clk(Deteccion_Palanca), .D(1'b1), .Q(Salida), .preset(1'b0), .en(1'b1), .reset(not_1_out));  // open: Qn
  not not_1 (not_1_out, Habilitar);
  and and_2 (Influye, Salida, Habilitar);
endmodule

module controlador_animacion (
  input  Palanca,
  output Display_1,
  output Display_2,
  output Display_3
);

  wire clock_1_out, comparator_1_eq, comparator_1_gt, comparator_2_eq, comparator_2_gt, comparator_3_eq,
       comparator_3_gt;
  wire [2:0] counter_1_q;

  Counter #(.width(3), .max('h7), .ongoal("stay")) counter_1 (
    .Q(counter_1_q), .clk(clock_1_out), .clr(Palanca));  // open: load, D, count, carry
  Clock clock_1 (.out(clock_1_out));
  Comparator #(.width(3), .mode("unsigned")) comparator_1 (
    .a(counter_1_q), .b(3'b101), .gt(comparator_1_gt), .eq(comparator_1_eq));  // open: lt
  Comparator #(.width(3), .mode("unsigned")) comparator_2 (
    .a(counter_1_q), .b(3'b110), .gt(comparator_2_gt), .eq(comparator_2_eq));  // open: lt
  Comparator #(.width(3), .mode("unsigned")) comparator_3 (
    .a(counter_1_q), .b(3'b111), .gt(comparator_3_gt), .eq(comparator_3_eq));  // open: lt
  or or_1 (Display_1, comparator_1_gt, comparator_1_eq);
  or or_2 (Display_2, comparator_2_gt, comparator_2_eq);
  or or_3 (Display_3, comparator_3_gt, comparator_3_eq);

  // Notes on the sheet:
  //   Tiempo
  //   Animacion
  //   Detener 1
  //   tiempo ≥ 5
  //   Detener 2
  //   tiempo ≥ 6
  //   Detener 3
endmodule

module generador_resultados (
  input  Generar,
  input  Reloj,
  output [1:0] out_3
);

  wire and_1_out, and_2_out, comparator_1_eq, not_1_out, not_2_out, or_1_out, register_1_q;
  wire [1:0] random_1_out;

  or or_1 (or_1_out, and_2_out, Generar);
  Register #(.width(1)) register_1 (.D(or_1_out), .en(1'b1), .Q(register_1_q), .clk(Reloj));  // open: clr
  not not_1 (not_1_out, Generar);
  Random #(.width(2), .seed(1)) random_1 (.clk(Reloj), .out(random_1_out));  // open: next, clr
  and and_1 (and_1_out, register_1_q, not_1_out, not_2_out);
  Comparator #(.width(2)) comparator_1 (.a(random_1_out), .b(2'b11), .eq(comparator_1_eq));  // open: gt, lt
  and and_2 (and_2_out, register_1_q, comparator_1_eq);
  not not_2 (not_2_out, comparator_1_eq);
  Register #(.width(2)) register_2 (.D(random_1_out), .en(and_1_out), .Q(out_3), .clk(Reloj));  // open: clr

  // Notes on the sheet:
  //   Buscando
  //   Generar
endmodule

module maquina_estados (
  input  Reloj,
  input  Victoria_Terminada,
  input  Nueva_Tirada,
  input  Hay_Creditos,
  input  Animacion_Terminada,
  input  Hay_Premio,
  output out_7,
  output out_8
);

  wire and_1_out, and_2_out, and_3_out, and_4_out, and_5_out, not_1_out, not_2_out, not_3_out, not_4_out,
       not_5_out, not_6_out, not_7_out, or_1_out, or_2_out, or_3_out;

  not not_1 (not_1_out, Animacion_Terminada);
  or or_1 (or_1_out, not_1_out, Hay_Premio);
  not not_2 (not_2_out, Victoria_Terminada);
  not not_3 (not_3_out, out_7);
  not not_4 (not_4_out, out_7);
  not not_5 (not_5_out, out_8);
  not not_6 (not_6_out, out_7);
  not not_7 (not_7_out, Victoria_Terminada);
  and and_1 (and_1_out, out_7, out_8, not_2_out);
  and and_2 (and_2_out, Animacion_Terminada, Hay_Premio, out_8, not_3_out);
  and and_3 (and_3_out, not_4_out, or_1_out, out_8);
  and and_4 (and_4_out, not_5_out, not_6_out, Nueva_Tirada, Hay_Creditos);
  and and_5 (and_5_out, out_8, out_7, not_7_out);
  or or_2 (or_2_out, and_1_out, and_2_out);
  or or_3 (or_3_out, and_3_out, and_4_out, and_5_out);
  D_Flip_Flop A (.clk(Reloj), .D(or_2_out), .Q(out_7));  // open: Qn, preset, en, reset
  D_Flip_Flop B (.clk(Reloj), .D(or_3_out), .Q(out_8));  // open: Qn, preset, en, reset

  // Other names for the same wires on the sheet: R = Reloj

  // Notes on the sheet:
  //   /AT*HP
  //   B
  //   Q  *Q  */VT
  //   A
  //   AT*HP*Q  */Q
  //   B
  //   (/AT+HP)*/Q  *Q  
  //   A
  //   /Q  */Q  *NT*HC
  //   B
  //   B
  //   Q  *Q  */VT
  //   A
  //   A
  //   A
  //   B
endmodule

module control_juego (
  input  in_1,
  input  in_2
);

  // OR_Gate or_1 has open pins: in0=in_1, in1=in_2, out=open
endmodule

module controlador_creditos (
  input  Jugar,
  input  [7:0] Premio,
  input  Cobrar,
  output [7:0] Saldo_Actual,
  output Hay_Creditos
);

  wire C, inicializador_q;
  wire [7:0] adder_1_out, multiplexer_1_out, multiplexer_2_out, register_1_q, subtractor_1_out;

  Clock clock_1 (.out(C));
  Subtractor subtractor_1 (.a(Saldo_Actual), .b(8'h1), .out(subtractor_1_out));  // open: bin, bout
  Adder adder_1 (.a(Saldo_Actual), .b(Premio), .out(adder_1_out));  // open: cin, cout
  Multiplexer #(.width(8)) multiplexer_1 (
    .in0(Saldo_Actual), .in1(subtractor_1_out), .out(multiplexer_1_out), .sel(Jugar), .en(1'b1));
  Multiplexer #(.width(8)) multiplexer_2 (
    .in0(multiplexer_1_out), .in1(adder_1_out), .out(multiplexer_2_out), .sel(Cobrar), .en(1'b1));
  Register register_1 (.D(multiplexer_2_out), .Q(register_1_q), .clk(C));  // open: en, clr
  Multiplexer #(.width(8)) multiplexer_3 (
    .in0(8'h3), .in1(register_1_q), .out(Saldo_Actual), .sel(inicializador_q), .en(1'b1));
  D_Flip_Flop inicializador (.clk(C), .D(1'b1), .Q(inicializador_q));  // open: Qn, preset, en, reset
  Comparator #(.mode("unsigned")) comparator_1 (.a(Saldo_Actual), .b({8{1'b0}}), .gt(Hay_Creditos));  // open: eq, lt
endmodule
